# Fritzing sketch larm (saved by Fritzing 0.9.3b)
breadboards: 1

parts:
  Part1 = Arduino Uno (Rev3)
  S1 = Pushbutton [package="[THT]"]
  S2 = Pushbutton [package="[THT]"]
  S3 = Pushbutton [package="[THT]"]
  R1 = Resistor [tolerance=±5% resistance=220 package=THT]
  R2 = Resistor [tolerance=±5% resistance=220 package=THT]
  LED1 = LED - 5mm [color="Red (633nm)" package="5 mm [THT]"]
  LED2 = LED - 5mm [color="Green (555nm)" package="5 mm [THT]"]

nets:
  N1: Part1.D12/MISO, LED1.anode
  N2: Part1.D13/SCK, LED2.anode
  N3: Part1.GND, S1.Pin_1, S1.Pin_2, S2.Pin_1, S2.Pin_2, S3.Pin_1, S3.Pin_2, R1.Pin_1, R2.Pin_1
  N4: Part1.D2, S2.Pin_3, S2.Pin_4
  N5: Part1.D3_PWM, S1.Pin_3, S1.Pin_4
  N6: Part1.D4, S3.Pin_3, S3.Pin_4
